# Fritzing sketch watersensor (saved by Fritzing 0.8.3b)
breadboards: 1

parts:
  Part1 = Arduino Leonardo (Rev3b)
  R1 = Resistor [tolerance=±5% resistance=100k package=THT]
  R2 = Resistor [tolerance=±5% resistance=100k package=THT]
  R3 = Resistor [tolerance=±5% resistance=100k package=THT]
  R4 = Resistor [tolerance=±5% resistance=100k package=THT]
  R5 = Resistor [tolerance=±5% resistance=100k package=THT]
  R6 = Resistor [tolerance=±5% resistance=100k package=THT]
  R7 = Resistor [tolerance=±5% resistance=100k package=THT]
  R8 = Resistor [tolerance=±5% resistance=100k package=THT]
  R9 = Resistor [tolerance=±5% resistance=100k package=THT]
  R10 = Resistor [tolerance=±5% resistance=100k package=THT]
  R11 = Slide Potentiometer [maximum_resistance=100kΩ]
  R12 = Slide Potentiometer [maximum_resistance=100kΩ]

nets:
  N1: Part1.D2/SDA, R3.Pin_1, R11.leg1
  N2: Part1.D3_PWM/SCL, R4.Pin_1
  N3: Part1.D4/A6, R2.Pin_1
  N4: Part1.D5_PWM, R9.Pin_1
  N5: Part1.D6_PWM/A7, R5.Pin_1
  N6: Part1.D7, R6.Pin_1
  N7: Part1.5V, R11.wiper, R12.wiper
  N8: Part1.D8/A8, R7.Pin_1
  N9: Part1.D9_PWM/A9, R8.Pin_1
  N10: Part1.D10_PWM/A10, R10.Pin_1
  N11: Part1.D11_PWM, R1.Pin_1, R12.leg1
  N12: Part1.GND, R1.Pin_0, R2.Pin_0, R3.Pin_0, R4.Pin_0, R5.Pin_0, R6.Pin_0, R7.Pin_0, R8.Pin_0, R9.Pin_0, R10.Pin_0

notes:
  BLEmini Tx
  BLEmini Rx
  BLEmini GND
  BLEmini Vin
  "level sensors"
